# Fritzing sketch bread (saved by Fritzing 0.9.3b)
breadboards: 2

parts:
  U1 = LuaNode32 / ESP32 [part_number=ESP32S-PIN30]
  LED1 = smd LED [color="Red (633nm)" package="0805 [SMD]"]
  Mod1 = KY-019 5V Relay Module [package="Breakout board"]
  T1 = LM34 Temperature Sensor [package="TO92 [THT]"]
  Part1 = Ambient Light Sensor (TEMT6000 Breakout Board)

nets:
  N1: U1.D35, T1.Vout
  N2: U1.D32, Part1.S
  N3: U1.D25, Mod1.S
  N4: U1.D26, LED1.anode
  GND: U1.GND, LED1.cathode, Mod1.-, T1.GND, Part1.GND
  3V3: U1.3V3, Mod1.+, T1.+Vs, Part1.VCC

custom parts:
  LuaNode32 / ESP32: New Image for LuaNode32 DOIT ESP32 DEVKIT V1. Base parts from LuaNode32 / ESP32 ESP32 based LuaNode32 by G.Noorlander DOIT Esp32 DevKit v1 (30 pins long, 11 pins width) by Werner Rothschopf (modified by vanepp Dec 2018)
  KY-019 5V Relay Module: KY-019 5V Relay module, used to control AC circuits. (Special thanks to vanepp for fixing the PCB holes and other errors)
